# Fritzing sketch Missile Command (saved by Fritzing 0.9.3b)
breadboards: 1

parts:
  Part1 = Arduino Uno (Rev3)
  R1 = Resistor [tolerance=±5% resistance=220 package=THT]
  R2 = Resistor [tolerance=±5% resistance=220 package=THT]
  R3 = Resistor [tolerance=±5% resistance=220 package=THT]
  LED19 = LED - 3mm [color="Red (633nm)" package="3 mm [THT]"]
  LED20 = LED - 3mm [color="Red (633nm)" package="3 mm [THT]"]
  LED21 = LED - 3mm [color="Red (633nm)" package="3 mm [THT]"]
  LED22 = LED - 3mm [color="Red (633nm)" package="3 mm [THT]"]
  LED23 = LED - 3mm [color="Red (633nm)" package="3 mm [THT]"]
  LED24 = LED - 3mm [color="Red (633nm)" package="3 mm [THT]"]
  LED25 = LED - 3mm [color="Red (633nm)" package="3 mm [THT]"]
  LED26 = LED - 3mm [color="Red (633nm)" package="3 mm [THT]"]
  LED27 = LED - 3mm [color="Red (633nm)" package="3 mm [THT]"]
  LED28 = LED - 3mm [color="Red (633nm)" package="3 mm [THT]"]
  LED29 = LED - 3mm [color="Red (633nm)" package="3 mm [THT]"]
  LED30 = LED - 3mm [color="Red (633nm)" package="3 mm [THT]"]
  LED31 = LED - 3mm [color="Red (633nm)" package="3 mm [THT]"]
  LED32 = LED - 3mm [color="Red (633nm)" package="3 mm [THT]"]
  LED33 = LED - 3mm [color="Red (633nm)" package="3 mm [THT]"]
  LED34 = LED - 3mm [color="Red (633nm)" package="3 mm [THT]"]
  LED35 = LED - 3mm [color="Red (633nm)" package="3 mm [THT]"]
  LED36 = LED - 3mm [color="Red (633nm)" package="3 mm [THT]"]
  LED37 = LED - 3mm [color="Red (633nm)" package="3 mm [THT]"]
  LED38 = LED - 3mm [color="Red (633nm)" package="3 mm [THT]"]
  LED39 = LED - 3mm [color="Red (633nm)" package="3 mm [THT]"]
  LED40 = LED - 3mm [color="Red (633nm)" package="3 mm [THT]"]
  LED41 = LED - 3mm [color="Red (633nm)" package="3 mm [THT]"]
  LED42 = LED - 3mm [color="Red (633nm)" package="3 mm [THT]"]
  LED43 = LED - 3mm [color="Red (633nm)" package="3 mm [THT]"]
  U1 = SN74LS32N [package="DIP14 [THT]"]
  S1 = Momentary Switch [package=ksa_sealed_tac_switch]
  S2 = Momentary Switch [package=ksa_sealed_tac_switch]
  S3 = Momentary Switch [package=ksa_sealed_tac_switch]
  R4 = Resistor [tolerance=±5% resistance=220 package="2010 [SMD]"]
  R5 = Resistor [tolerance=±5% resistance=1k package="2010 [SMD]"]
  R6 = Resistor [tolerance=±5% resistance=1k package="2010 [SMD]"]
  SP1 = SPEAKER [package=pcb_mount_speaker]

nets:
  N1: Part1.A0, U1.3A, U1.4A, U1.4B, S1.3, S2.3, S3.3, R6.Pin_0
  N2: Part1.A1, SP1.-
  N3: Part1.D8, LED22.cathode, LED30.cathode, LED38.cathode
  N4: Part1.D9_PWM, LED20.cathode, LED21.cathode, LED29.cathode, LED37.cathode
  N5: Part1.D10_PWM/SS, LED19.cathode, LED28.cathode, LED36.cathode
  N6: Part1.D11_PWM/MOSI, R1.Pin_0
  N7: Part1.D12/MISO, R2.Pin_0
  N8: Part1.D13/SCK, R3.Pin_0
  N9: Part1.D2, U1.1Y
  N10: Part1.D3_PWM, LED27.cathode, LED35.cathode, LED41.cathode
  N11: Part1.D4, LED26.cathode, LED34.cathode, LED43.cathode
  N12: Part1.D5_PWM, LED24.cathode, LED32.cathode, LED42.cathode
  N13: Part1.D6_PWM, LED25.cathode, LED33.cathode, LED40.cathode
  N14: Part1.D7, LED23.cathode, LED31.cathode, LED39.cathode
  N15: Part1.5V, S1.2, R4.Pin_0, R5.Pin_0
  N16: R1.Pin_1, LED19.anode, LED20.anode, LED21.anode, LED22.anode, LED23.anode, LED24.anode, LED25.anode, LED26.anode, LED27.anode
  N17: R2.Pin_1, LED28.anode, LED29.anode, LED30.anode, LED31.anode, LED32.anode, LED33.anode, LED34.anode, LED35.anode
  N18: R3.Pin_1, LED36.anode, LED37.anode, LED38.anode, LED39.anode, LED40.anode, LED41.anode, LED42.anode, LED43.anode
  N19: U1.1A, U1.4Y
  N20: U1.1B, U1.3Y
  N21: U1.3B, R6.Pin_1, SP1.+
  N22: S2.2, R4.Pin_1
  N23: S3.2, R5.Pin_1
